# Fritzing sketch 02_Press_to_turn_on (saved by Fritzing 0.9.3b)
breadboards: 1

parts:
  WeMos_D1_Mini1 = WeMos D1 Mini  # not connected
  R1 = Resistor [tolerance=±5% resistance=220 package=THT]
  LED1 = LED - 5mm [color="Red (633nm)" package="5 mm [THT]"]
  S1 = Pushbutton [package="[THT]"]

nets:
  N1: R1.Pin_0, LED1.anode
  N2: LED1.cathode, S1.Pin_3, S1.Pin_4
  N3: S1.Pin_1, S1.Pin_2
