# Fritzing sketch rc (saved by Fritzing 0.9.3b)

parts:
  WeMos_D1_Mini1 = WeMos D1 Mini
  M1 = Dagu DGServo 9g (Top view) [part_number=RS001B]

nets:
  3V3: WeMos_D1_Mini1.3V3, M1.vcc
  N1: WeMos_D1_Mini1.D8, M1.pulse
  N2: WeMos_D1_Mini1.G, M1.gnd
