# Fritzing sketch sensors (saved by Fritzing 0.9.3b)
breadboards: 1

parts:
  WeMos_D1_Mini1 = WeMos D1 Mini  # not connected
  R1 = Resistor [tolerance=±5% resistance=220 package=THT]
  R2 = Photocell (LDR) [package=THT]
  RHT1 = Humidity and Temperature Sensor RHT03

nets:
  N1: R1.Pin_0, RHT1.Vcc
  N2: R1.Pin_1, R2.pin_1
  N3: R2.pin_0, RHT1.GND_2
